# Fritzing sketch sketch (saved by Fritzing 0.9.3b)

parts:
  Raspberry_Pi1 = Raspberry Pi 2
  Part1 = 16 NeoPixel Ring [part_number=1463]
  JACK1 = 2.1mm Barrel Jack with Terminal Block
  J1 = Basic Servo

nets:
  N1: Raspberry_Pi1.GPIO18, Part1.IN
  GND: Raspberry_Pi1.GND, Part1.GND
  5V: Raspberry_Pi1.5V, Part1.VDD
  N2: JACK1.POS, J1.gnd
  N3: JACK1.NEG, J1.vcc

custom parts:
  16 NeoPixel Ring: 16 ultra bright smart LED NeoPixels are arranged in a circle with 1.75" (44.5mm) outer diameter. The rings are 'chainable' - connect the output pin of one to the input pin of another. Use only one microcontroller pin to control as many as you can chain together! Each LED is addressable as the driver chip is inside the LED. Each one has ~18mA constant current drive so the color will be very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
